# Fritzing sketch Semaforo (saved by Fritzing 0.9.3b)
breadboards: 1

parts:
  Componente1 = Arduino Uno (Rev3)
  R1 = Resistor [tolerance=±5% resistance=220 package=THT]
  LED1 = LED - 5mm [color="Red (633nm)" package="5 mm [THT]"]
  LED2 = LED - 5mm [color="Green (565nm)" package="5 mm [THT]"]
  R2 = Resistor [tolerance=±5% resistance=220 package=THT]

nets:
  N1: Componente1.D13/SCK, R2.Pin_1
  N2: Componente1.GND, LED1.cathode, LED2.cathode
  N3: R1.Pin_0, LED1.anode
  N4: LED2.anode, R2.Pin_0
